# Fritzing sketch xiaesp32-c3-voice-agent (saved by Fritzing 1.0.7)
breadboards: 1

parts:
  J3 = female pin header, 3 pins [form="♀ (female)"]
  J4 = female pin header, 3 pins [form="♀ (female)"]
  J2 = female pin header, 7 pins [form="♀ (female)"]
  J1 = female pin header, 7 pins [form="♀ (female)"]
  J5 = female pin header, 7 pins [form="♀ (female)"]
  U1 = XIAO ESP32C3

nets:
  N1: J3.pin1, J4.pin1, J2.pin2, J5.pin6, U1.GND
  N2: J3.pin2, J2.pin3, J5.pin5, U1.3V3
  N3: J3.pin3, J1.pin3, U1.D2
  N4: J4.pin2, J1.pin4, J5.pin1, U1.D3
  N5: J4.pin3, J1.pin2, J5.pin2, U1.D1
  N6: J2.pin1, J5.pin7, U1.5V
  N7: J2.pin4, U1.D10
  N8: J2.pin5, U1.D9
  N9: J2.pin6, U1.D8
  N10: J2.pin7, U1.D7
  N11: J1.pin1, J5.pin3, U1.D0
  N12: J1.pin5, U1.D4
  N13: J1.pin6, U1.D5
  N14: J1.pin7, U1.D6

custom parts:
  XIAO ESP32C3: Seeed Studio XIAO ESP32C3 adopts new RISC-V architecture, supporting both Wi-Fi and BLE wireless connectivities. For Internet of Things applications, you will find it is flexible and suitable for all kinds of IoT scenarios.
