# Fritzing sketch xiaesp32-c6-voice-agent (saved by Fritzing 1.0.7)
breadboards: 1

parts:
  J3 = female pin header, 3 pins [form="♀ (female)"]
  J4 = female pin header, 3 pins [form="♀ (female)"]
  J2 = female pin header, 7 pins [form="♀ (female)"]
  J1 = female pin header, 7 pins [form="♀ (female)"]
  J5 = female pin header, 7 pins [form="♀ (female)"]

nets:
  N1: J3.pin1, J4.pin1, J2.pin2, J5.pin6
  N2: J3.pin2, J2.pin3, J5.pin5
  N3: J3.pin3, J1.pin3
  N4: J4.pin2, J1.pin4, J5.pin1
  N5: J4.pin3, J1.pin2, J5.pin2
  N6: J2.pin1, J5.pin7
  N7: J1.pin1, J5.pin3
