# Fritzing sketch xiaesp32-s3-voice-agent (saved by Fritzing 1.0.7)
breadboards: 1

parts:
  J3 = female pin header, 3 pins [form="♀ (female)"]
  J4 = female pin header, 3 pins [form="♀ (female)"]
  J2 = female pin header, 7 pins [form="♀ (female)"]
  J1 = female pin header, 7 pins [form="♀ (female)"]
  J5 = female pin header, 7 pins [form="♀ (female)"]
  XIAO_ESP32S1 = XIAO ESP32S3 [package="DIP (Dual Inline) [THT]"]
  Part1 = INMP441
  Part2 = Adafruit MAX98357A I2S 3W Class D Amplifier [part_number="Adafruit #3006"]

nets:
  GND: J3.pin1, J4.pin1, J2.pin2, J5.pin6, XIAO_ESP32S1.GND, Part1.L/R, Part1.GND, Part2.GND
  3V3: J3.pin2, J2.pin3, J5.pin5, XIAO_ESP32S1.3V3, Part1.VDD, Part2.SD_MODE
  N1: J3.pin3, J1.pin3, XIAO_ESP32S1.D2, Part1.SD
  N2: J4.pin2, J1.pin4, J5.pin1, XIAO_ESP32S1.D3, Part1.WS, Part2.LRCLK
  N3: J4.pin3, J1.pin2, J5.pin2, XIAO_ESP32S1.D1, Part1.SCK, Part2.BCLK
  5V: J2.pin1, J5.pin7, XIAO_ESP32S1.5V, Part2.VIN
  N4: J2.pin4, XIAO_ESP32S1.D10
  N5: J2.pin5, XIAO_ESP32S1.D9
  N6: J2.pin6, XIAO_ESP32S1.D8
  N7: J2.pin7, XIAO_ESP32S1.D7
  N8: J1.pin1, J5.pin3, XIAO_ESP32S1.D0, Part2.DIN
  N9: J1.pin5, XIAO_ESP32S1.D4
  N10: J1.pin6, XIAO_ESP32S1.D5
  N11: J1.pin7, XIAO_ESP32S1.D6
  N12: J5.pin4, Part2.GAIN

custom parts:
  XIAO ESP32S3: Seeed Studio XIAO ESP32S3 leverages 240MHz Xtensa 32-bit LX7 dual-core processor, supporting both WiFi and BLE 5.0 wireless connectivities, a 2.4GHz Rod antenna, allows for deep sleep mode with power consumption as low as 14μA while supporting lithium battery charging management. Ideal for the Internet of Things, Smart Homes, Wireless wearable devices, Robotics, etc.
  INMP441: This is a simple breakout board for the INMP441 I2S MEMS microphone.
  Adafruit MAX98357A I2S 3W Class D Amplifier: Listen to this good news - we now have an all in one digital audio amp breakout board that works incredibly well with the Raspberry Pi! If you're looking for an easy and low cost way to get you digital sound files bumpin' then the MAX08357 I2S Amp Breakout is for you. It takes standard I2S digital audio input and, not only decodes it into analog, but also amplifies it directly into a speaker.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
