# Fritzing sketch esp32c3-voice-agent (saved by Fritzing 1.0.7)
breadboards: 1

parts:
  U1 = XIAO ESP32C3
  Part1 = INMP441
  Part2 = Adafruit MAX98357A I2S 3W Class D Amplifier [part_number="Adafruit #3006"]

nets:
  N1: U1.D0, Part2.DIN
  N2: U1.D1, Part1.SCK, Part2.BCLK
  N3: U1.D2, Part1.SD
  N4: U1.D3, Part1.WS, Part2.LRCLK
  3V3: U1.3V3, Part1.VDD, Part2.SD_MODE
  GND: U1.GND, Part1.L/R, Part1.GND, Part2.GND
  5V: U1.5V, Part2.VIN

custom parts:
  XIAO ESP32C3: Seeed Studio XIAO ESP32C3 adopts new RISC-V architecture, supporting both Wi-Fi and BLE wireless connectivities. For Internet of Things applications, you will find it is flexible and suitable for all kinds of IoT scenarios.
  INMP441: This is a simple breakout board for the INMP441 I2S MEMS microphone.
  Adafruit MAX98357A I2S 3W Class D Amplifier: Listen to this good news - we now have an all in one digital audio amp breakout board that works incredibly well with the Raspberry Pi! If you're looking for an easy and low cost way to get you digital sound files bumpin' then the MAX08357 I2S Amp Breakout is for you. It takes standard I2S digital audio input and, not only decodes it into analog, but also amplifies it directly into a speaker.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
